# Fritzing sketch esquemaConexion (saved by Fritzing 0.9.3b)

parts:
  Mod1 = Nano-V3-0-IO-Expansion-Adapter
  Componente1 = Arduino Nano (Rev3.0)
  LED1 = RGB LED (com. anode, rbg) [package="5 mm [THT]"]
  J1 = Basic Servo  # not connected
  J2 = Piezo Speaker  # not connected
  J3 = Piezo Speaker  # not connected
  U1 = SWITCH-SPST-2 [package=r_sw_th]
  VCC1 = 4 x AAA Battery Mount

nets:
  N1: Mod1.RST, Componente1.RESET
  VCC: Mod1.VCC, Componente1.5V, U1.P
  VIN: Mod1.VIN, Componente1.VIN
  N2: Mod1.A0, Componente1.A0
  N3: Mod1.A1, Componente1.A1
  N4: Mod1.A2, Componente1.A2
  N5: Mod1.A3, Componente1.A3
  N6: Mod1.A6, Componente1.A6
  N7: Mod1.A7, Componente1.A7
  N8: Mod1.D13/SCK, Componente1.D13/SCK
  N9: Mod1.NC, Componente1.3V3
  N10: Mod1.AREF, Componente1.AREF
  N11: Mod1.A4/SDA, Componente1.A4
  N12: Mod1.A5/SCL, Componente1.A5
  GND: Mod1.GND, Componente1.GND
  N13: Mod1.D12/MISO, Componente1.D12/MISO
  N14: Mod1.D11_PWM/MOSI, Componente1.D11/MOSI
  N15: Mod1.D10_PWM/SS, Componente1.D10
  N16: Mod1.D9_PWM, Componente1.D9
  N17: Mod1.D8, Componente1.D8
  N18: Mod1.D7, Componente1.D7
  N19: Mod1.D6_PWM, Componente1.D6, LED1.green_cathode
  N20: Mod1.D5_PWM, Componente1.D5, LED1.blue_cathode
  N21: Mod1.D4, Componente1.D4
  N22: Mod1.D3_PWM, Componente1.D3, LED1.red_cathode
  N23: Mod1.D2, Componente1.D2
  N24: Mod1.D0/RX#64, Mod1.D1/TX#129, Componente1.D0/RX
  N25: Mod1.D1/TX#65, Mod1.D0/RX#128, Componente1.D1/TX
  N26: U1.O, VCC1.+

notes:
  Piezoeléctrico sensor (A0)
  Servomotor (D9)
  Piezoeléctrico altavoz (D8)
  Rojo: D3
  Verde: D5
  Azul: D6

custom parts:
  Nano-V3-0-IO-Expansion-Adapter: Nano V3.0 IO Expansion Adapter Shield. Note pcb view has been supressed as not useful. You can drag a Nano over the Nano connectors and it will connect and appear in schematic (although at present due to a bug, routing will not show as complete in breadboard).
